# Fritzing sketch flash_pcb_millable (saved by Fritzing 0.9.2b)
circuit board: 4cm x 2cm
breadboards: 1

parts:
  ESP = ESP8266 WiFi Module [part_number=ESP8266]
  BOOT = Pushbutton [package=THT]
  RST = Pushbutton [package=THT]
  LED1 = LED - 5mm [color="Red (633nm)" package="5 mm [THT]"]
  R1 = Resistor [tolerance=±10% resistance=220 package=THT]
  G-FTDI = FTDI Basic Programmer
  JP1 = Header 2 [package=jst-2-smd]

nets:
  N1: ESP.RXD, G-FTDI.TXO
  N2: ESP.VCC, ESP.CH_PD, R1.Pin_0, G-FTDI.POWER, JP1.1
  N3: ESP.GPIO_0, BOOT.leg0
  N4: ESP.RST, RST.leg0, LED1.cathode
  GND: ESP.GND, BOOT.leg1, RST.leg1, G-FTDI.GND, JP1.2
  N5: ESP.TXD, G-FTDI.RXI
  N6: LED1.anode, R1.Pin_1

notes:
  Flash v9
  GND

custom parts:
  ESP8266 WiFi Module: Generic WiFi Module based on the ESP8266 with onboard PCB antenna and UART communications
